# Fritzing sketch TITAN routing board (saved by Fritzing 0.9.3b)
circuit board: 10.0002cm x 10cm
breadboards: 1

parts:
  J8 = male pin header, 6 pins [form="♂ (male)"]
  J6 = male pin header, 6 pins [form="♂ (male)"]
  J4 = male pin header, 6 pins [form="♂ (male)"]
  J17 = double row male pin header, 24 pins [form="♂ (male)"]
  J16 = double row male pin header, 8 pins [form="♂ (male)"]
  J1 = male pin header, 6 pins [form="♂ (male)"]
  J5 = male pin header, 6 pins [form="♂ (male)"]
  J3 = male pin header, 6 pins [form="♂ (male)"]
  J13 = male pin header, 6 pins [form="♂ (male)"]
  J15 = male pin header, 8 pins [form="♂ (male)"]
  J12 = male pin header, 6 pins [form="♂ (male)"]
  J14 = male pin header, 8 pins [form="♂ (male)"]
  J9 = double row male pin header, 24 pins [form="♂ (male)"]
  IC1 = Voltage Regulator [package=to220-igo]
  J18 = Power Jack [package=power_jack_pth]
  Digital = male pin header, 14 pins [form="♂ (male)"]
  ATmega_328 = atmega328 [package=dip]
  Source = male pin header, 4 pins [form="♂ (male)"]
  RESET = SWITCH-MOMENTARY-2 [package=tactile_switch_tall]
  R4 = Resistor [tolerance=±5% resistance=10k package="0603 [SMD]"]
  Analog = male pin header, 7 pins [form="♂ (male)"]

nets:
  N1: J8.pin1, J9.pin24
  N2: J8.pin2, J13.pin1
  N3: J8.pin3, J13.pin2
  N4: J8.pin4, J9.pin23
  N5: J8.pin5, J9.pin22
  N6: J8.pin6, J9.pin21
  N7: J6.pin1, J9.pin20
  N8: J6.pin2, J13.pin3
  N9: J6.pin3, J13.pin4
  N10: J6.pin4, J9.pin19
  N11: J6.pin5, J9.pin18
  N12: J6.pin6, J9.pin17
  N13: J4.pin1, J9.pin4
  N14: J4.pin2, J9.pin3
  N15: J4.pin3, J9.pin2
  N16: J4.pin4, J12.pin2
  N17: J4.pin5, J12.pin1
  N18: J4.pin6, J9.pin1
  N19: J17.pin1, J15.pin1
  N20: J17.pin2, J15.pin2
  N21: J17.pin3, J15.pin3
  N22: J17.pin4, J15.pin4
  N23: J17.pin5, J14.pin1
  N24: J17.pin6, J14.pin2
  N25: J17.pin7, J14.pin3
  N26: J17.pin8, J14.pin4
  N27: J17.pin9, J14.pin5
  N28: J17.pin10, J14.pin6
  N29: J17.pin11, J14.pin7
  N30: J17.pin12, J14.pin8
  N31: J17.pin13, J16.pin4
  N32: J17.pin14, J16.pin3
  N33: J17.pin15, J16.pin2
  N34: J17.pin16, J16.pin1
  N35: J17.pin17, J16.pin8
  N36: J17.pin18, J16.pin7
  N37: J17.pin19, J16.pin6
  N38: J17.pin20, J16.pin5
  N39: J17.pin21, J15.pin5
  N40: J17.pin22, J15.pin6
  N41: J17.pin23, J15.pin7
  N42: J17.pin24, J15.pin8
  N43: J1.pin1, J9.pin12
  N44: J1.pin2, J9.pin11
  N45: J1.pin3, J9.pin10
  N46: J1.pin4, J12.pin6
  N47: J1.pin5, J12.pin5
  N48: J1.pin6, J9.pin9
  N49: J5.pin1, J9.pin16
  N50: J5.pin2, J13.pin5
  N51: J5.pin3, J13.pin6
  N52: J5.pin4, J9.pin15
  N53: J5.pin5, J9.pin14
  N54: J5.pin6, J9.pin13
  N55: J3.pin1, J9.pin8
  N56: J3.pin2, J9.pin7
  N57: J3.pin3, J9.pin6
  N58: J3.pin4, J12.pin4
  N59: J3.pin5, J12.pin3
  N60: J3.pin6, J9.pin5
  GND: IC1.GND, J18.GND, J18.GNDBREAK
  N61: IC1.IN, J18.PWR
  N62: IC1.OUT, Source.pin1, R4.Pin_1
  N63: Digital.pin1, ATmega_328.D0_(RX)
  N64: Digital.pin2, ATmega_328.D1_(TX)
  N65: Digital.pin3, ATmega_328.D2
  N66: Digital.pin4, ATmega_328.D3_(PWM)
  N67: Digital.pin5, ATmega_328.D4
  N68: Digital.pin6, ATmega_328.D5_(PWM)
  N69: Digital.pin7, ATmega_328.D6_(PWM)
  N70: Digital.pin8, ATmega_328.D7
  N71: Digital.pin9, ATmega_328.D8
  N72: Digital.pin10, ATmega_328.D9_(PWM)
  N73: Digital.pin11, ATmega_328.D10_(PWM)
  N74: Digital.pin12, ATmega_328.D11_(PWM)
  N75: Digital.pin13, ATmega_328.D12
  N76: Digital.pin14, ATmega_328.D13
  N77: ATmega_328.RESET, RESET.2, R4.Pin_0
  N78: ATmega_328.AREF, Analog.pin1
  N79: ATmega_328.A0, Analog.pin2
  N80: ATmega_328.A1, Analog.pin3
  N81: ATmega_328.A2, Analog.pin4
  N82: ATmega_328.A3, Analog.pin5
  N83: ATmega_328.A4, Analog.pin6
  N84: ATmega_328.A5, Analog.pin7
  N85: Source.pin3, Source.pin4, RESET.1

notes:
  UFSM 2019
  A0
  12
  A2
  A1
  A5
  A4
  A3
  5
  GND
  D0
  D6
  D3
  D5
  D1
  D4
  D9
  D2
  D7
  D8
  D10
  D11
  D12
  D13
  AREF
